# Fritzing sketch vibration_motor (saved by Fritzing 0.8.5b)
breadboards: 1

parts:
  Bauteil1 = Arduino Uno (Rev3)
  R1 = Rotary Potentiometer (Small) [maximum_resistance=100kΩ package=THT]
  Q1 = NPN-Transistor [package="TO92 [THT]"]
  U1 = Vibration Motor- ROB-08449 [package=vibe-motor-10mm]

nets:
  N1: Bauteil1.A0, R1.wiper
  N2: Bauteil1.D12/MISO, Q1.B
  N3: Bauteil1.GND, R1.leg2, U1.+
  N4: Bauteil1.3V3, R1.leg1, Q1.E
  N5: Q1.C, U1.-
